# Fritzing sketch MN-82 UPG A-Sheeld v.0.3 (на тахометре) (saved by Fritzing 1.0.6)
circuit board: 4cm x 4.8cm
breadboards: 8

parts:
  Q1 = PNP-Transistor [part_number=BC327-40 package="TO92 [THT]"]
  Q2 = PNP-Transistor [part_number=BC327-40 package="TO92 [THT]"]
  Q3 = PNP-Transistor [part_number=BC327-40 package="TO92 [THT]"]
  Q4 = PNP-Transistor [part_number=BC327-40 package="TO92 [THT]"]
  R2 = Resistor [tolerance=±5% resistance=1k power=0.25W package=THT]
  R3 = Resistor [tolerance=±5% resistance=1k power=0.25W package=THT]
  R5 = Resistor [tolerance=±5% resistance=1k power=0.25W package=THT]
  D1_1 = Arduino Pro Mini v13 [part_number="Arduino Pro MINI"]
  J2 = female pin header, 1 pin [form="♀ (female)" part_number=GND]
  R7 = Resistor [tolerance=±5% resistance=10k power=0.25W package=THT]
  R9 = Resistor [tolerance=±5% resistance=10k power=0.25W package=THT]
  J5 = female pin header, 5 pins [form="♀ (female)" part_number="вход от RX480-E-WQ"]
  C2 = Ceramic Capacitor [capacitance=100nF voltage=20V package="200 mil [THT, multilayer]"]
  C1 = Ceramic Capacitor [capacitance=100nF voltage=20V package="200 mil [THT, multilayer]"]
  R1 = Resistor [tolerance=±5% power=0.25W resistance=1k package=THT]
  R4 = Resistor [tolerance=±5% power=0.25W resistance=1k package=THT]
  Q5 = PNP-Transistor [part_number=BC327-40 package="TO92 [THT]"]
  R11 = Resistor [tolerance=±5% resistance=10k power=0.25W package=THT]
  J6 = female pin header, 1 pin [form="♀ (female)" part_number="hold pin"]
  R12 = Resistor [tolerance=±5% resistance=10k power=0.25W package=THT]
  R13 = Resistor [tolerance=±5% resistance=10k power=0.25W package=THT]
  R14 = Resistor [tolerance=±5% resistance=10k power=0.25W package=THT]
  R15 = Resistor [tolerance=±5% resistance=10k power=0.25W package=THT]
  J8 = female pin header, 1 pin [form="♀ (female)" part_number=Vcc]
  J3 = female pin header, 2 pins [form="♀ (female)"]
  J7 = female pin header, 2 pins [form="♀ (female)"]
  J9 = female pin header, 1 pin [form="♀ (female)" part_number=Vcc]
  J1 = female pin header, 5 pins [form="♀ (female)"]
  J4 = female alternating pin header, 2 pins [form="♀ (female)"]

nets:
  N1: Q1.E, Q2.E, Q3.E, Q4.E, D1_1.VCC, R7.Pin_0, R9.Pin_1, Q5.E, R11.Pin_0, R12.Pin_0, R13.Pin_0, R14.Pin_0, R15.Pin_0, J8.pin1, J9.pin1, J4.pin2
  N2: Q1.B, R1.Pin_1, R11.Pin_1
  N3: Q1.C, J1.pin1
  N4: Q2.B, R2.Pin_1, R12.Pin_1
  N5: Q2.C, J1.pin2
  N6: Q3.B, R3.Pin_1, R13.Pin_1
  N7: Q3.C, J1.pin3
  N8: Q4.B, R4.Pin_1, R14.Pin_1
  N9: Q4.C, J1.pin4
  N10: R2.Pin_0, D1_1.D5_PWM
  N11: R3.Pin_0, D1_1.D4
  N12: R5.Pin_0, D1_1.D9_PWM
  N13: R5.Pin_1, Q5.B, R15.Pin_1
  N14: D1_1.GND, J2.pin1, C2.1, C1.0, J3.pin1, J7.pin1, J4.pin1
  N15: D1_1.A2, R9.Pin_0, C2.0, J7.pin2
  N16: D1_1.A1, R7.Pin_1, C1.1, J3.pin2
  N17: D1_1.D13/SCK, J6.pin1
  N18: D1_1.D12/MISO, J5.pin5
  N19: D1_1.D11_PWM/MOSI, J5.pin2
  N20: D1_1.D10_PWM/SS, J5.pin1
  N21: D1_1.D8, J5.pin3
  N22: D1_1.D7, J5.pin4
  N23: D1_1.D6_PWM, R1.Pin_0
  N24: D1_1.D3_PWM, R4.Pin_0
  N25: Q5.C, J1.pin5

notes:
  Vcc
  GND
  VT
  D0
  D1
  D2
  D3
  Holl
  hold
  max 500mA
  к датчикам Холла A3144
  выход на диодные сборки
  GND Vcc

// code stored in the sketch: MN-82-A0-A3.ino
const int pinX = A0;
const int pinY = A1;

// ????? ???????? ?????????? (????? 0.5 ? ?? ??????? ??????)
const float MIN_VOLTAGE_THRESHOLD = 0.5; 

void setup() {
  Serial.begin(9600);
}

void loop() {
  // ?????? ???????? (????????? ????????????? ??? ?????? ??????????)
  int rawX = analogRead(pinX);
  int rawY = analogRead(pinY);

  // ????????? ? ???????? ?????? ?? ???????? ?????? (? ?????? ????????)
  float voltageX = (rawX * 5.0 / 1023.0) * 3.12;
  float voltageY = (rawY * 5.0 / 1023.0) * 3.12;

  Serial.print("?????????? X: "); Serial.print(voltageX, 1); Serial.print("V | ");
  Serial.print("?????????? Y: "); Serial.print(voltageY, 1); Serial.print("V -> ");

  // ?????????? ?????????
  if (voltageX > MIN_VOLTAGE_THRESHOLD && voltageY < MIN_VOLTAGE_THRESHOLD) {
    Serial.print("???????? ??????. ??????????? ??????????: ");
    Serial.concat(voltageX); Serial.println(" V");
  } 
  else if (voltageY > MIN_VOLTAGE_THRESHOLD && voltageX < MIN_VOLTAGE_THRESHOLD) {
    Serial.print("???????? ?????. ??????????? ??????????: ");
    Serial.concat(voltageY); Serial.println(" V");
  } 
  else if (voltageX > MIN_VOLTAGE_THRESHOLD && voltageY > MIN_VOLTAGE_THRESHOLD) {
    Serial.print("????? ?????????? / ??????????! ??????? X: ");
    Serial.print(voltageX, 1); Serial.print("V, ??????? Y: "); Serial.println(voltageY, 1);
  } 
  else {
    Serial.println("???? (????? ?????????)");
  }

  delay(300);
}
