# Fritzing sketch MN-82 UPG A-Sheeld версия с подтяжкой эмитера на печатке (saved by Fritzing 0.9.5d)
circuit board: 4cm x 4.8cm
breadboards: 8

parts:
  J1 = female pin header, 5 pins [form="♀ (female)" part_number="выход на диодные сборки"]
  Q1 = PNP-Transistor [part_number=BC327-40 package="TO92 [THT]"]
  Q2 = PNP-Transistor [part_number=BC327-40 package="TO92 [THT]"]
  Q3 = PNP-Transistor [part_number=BC327-40 package="TO92 [THT]"]
  Q4 = PNP-Transistor [part_number=BC327-40 package="TO92 [THT]"]
  R2 = Resistor [tolerance=±5% resistance=1k power=0.25W package=THT]
  R3 = Resistor [tolerance=±5% resistance=1k power=0.25W package=THT]
  R5 = Resistor [tolerance=±5% resistance=1k power=0.25W package=THT]
  J4 = female pin header, 2 pins [form="♀ (female)" part_number=Vcc]
  D1_1 = Arduino Pro Mini v13 [part_number="Arduino Pro MINI"]
  J2 = female pin header, 1 pin [form="♀ (female)" part_number="пины питания"]
  R7 = Resistor [tolerance=±5% resistance=4.7k power=0.25W package=THT]
  R8 = Resistor [tolerance=±5% resistance=10k power=0.25W package=THT]
  R9 = Resistor [tolerance=±5% resistance=4.7k power=0.25W package=THT]
  R10 = Resistor [tolerance=±5% resistance=10k power=0.25W package=THT]
  D2 = Zener Diode [part_number=1N4732A breakdown_voltage=4.7V package="300 mil [THT]"]
  D3 = Zener Diode [part_number=1N4732A breakdown_voltage=4.7V package="300 mil [THT]"]
  J5 = female pin header, 5 pins [form="♀ (female)" part_number="вход от RX480-E-WQ"]
  J3 = female pin header, 2 pins [form="♀ (female)" part_number="к полюсам мотора"]
  C2 = Ceramic Capacitor [capacitance=100nF voltage=20V package="200 mil [THT, multilayer]"]
  C1 = Ceramic Capacitor [capacitance=100nF voltage=20V package="200 mil [THT, multilayer]"]
  R1 = Resistor [tolerance=±5% power=0.25W resistance=1k package=THT]
  R4 = Resistor [tolerance=±5% power=0.25W resistance=1k package=THT]
  Q5 = PNP-Transistor [part_number=BC327-40 package="TO92 [THT]"]
  R11 = Resistor [tolerance=±5% resistance=10k package=THT]
  J6 = female pin header, 1 pin [form="♀ (female)" part_number="hold pin"]
  R12 = Resistor [tolerance=±5% resistance=10k package=THT]
  R13 = Resistor [tolerance=±5% resistance=10k package=THT]
  R14 = Resistor [tolerance=±5% resistance=10k package=THT]
  R15 = Resistor [tolerance=±5% resistance=10k package=THT]

nets:
  N1: J1.pin1, Q1.C
  N2: J1.pin2, Q2.C
  N3: J1.pin3, Q3.C
  N4: J1.pin4, Q4.C
  N5: J1.pin5, Q5.C
  N6: Q1.E, Q2.E, Q3.E, Q4.E, J4.pin2, D1_1.VCC, Q5.E, R11.Pin_0, R12.Pin_0, R13.Pin_0, R14.Pin_0, R15.Pin_0
  N7: Q1.B, R1.Pin_1, R11.Pin_1
  N8: Q2.B, R2.Pin_1, R12.Pin_1
  N9: Q3.B, R3.Pin_1, R13.Pin_1
  N10: Q4.B, R4.Pin_1, R14.Pin_1
  N11: R2.Pin_0, D1_1.D5_PWM
  N12: R3.Pin_0, D1_1.D4
  N13: R5.Pin_0, D1_1.D2
  N14: R5.Pin_1, Q5.B, R15.Pin_1
  N15: J4.pin1, D1_1.GND, J2.pin1, R7.Pin_0, R9.Pin_1, D2.anode, D3.anode, C2.1, C1.0
  N16: D1_1.A2, R9.Pin_0, R10.Pin_0, D2.cathode, C2.0
  N17: D1_1.A1, R7.Pin_1, R8.Pin_0, D3.cathode, C1.1
  N18: D1_1.D13/SCK, J6.pin1
  N19: D1_1.D12/MISO, J5.pin5
  N20: D1_1.D11_PWM/MOSI, J5.pin2
  N21: D1_1.D10_PWM/SS, J5.pin1
  N22: D1_1.D9_PWM, J5.pin3
  N23: D1_1.D8, J5.pin4
  N24: D1_1.D7, R1.Pin_0
  N25: D1_1.D3_PWM, R4.Pin_0
  N26: R8.Pin_1, J3.pin2
  N27: R10.Pin_1, J3.pin1

notes:
  Vcc
  GND
  VT
  D0
  D1
  D2
  D3
  -M+
  hold
  max 500mA

// code stored in the sketch: MN-82-A0-A3.ino
const int pinX = A0;
const int pinY = A1;

// ????? ???????? ?????????? (????? 0.5 ? ?? ??????? ??????)
const float MIN_VOLTAGE_THRESHOLD = 0.5; 

void setup() {
  Serial.begin(9600);
}

void loop() {
  // ?????? ???????? (????????? ????????????? ??? ?????? ??????????)
  int rawX = analogRead(pinX);
  int rawY = analogRead(pinY);

  // ????????? ? ???????? ?????? ?? ???????? ?????? (? ?????? ????????)
  float voltageX = (rawX * 5.0 / 1023.0) * 3.12;
  float voltageY = (rawY * 5.0 / 1023.0) * 3.12;

  Serial.print("?????????? X: "); Serial.print(voltageX, 1); Serial.print("V | ");
  Serial.print("?????????? Y: "); Serial.print(voltageY, 1); Serial.print("V -> ");

  // ?????????? ?????????
  if (voltageX > MIN_VOLTAGE_THRESHOLD && voltageY < MIN_VOLTAGE_THRESHOLD) {
    Serial.print("???????? ??????. ??????????? ??????????: ");
    Serial.concat(voltageX); Serial.println(" V");
  } 
  else if (voltageY > MIN_VOLTAGE_THRESHOLD && voltageX < MIN_VOLTAGE_THRESHOLD) {
    Serial.print("???????? ?????. ??????????? ??????????: ");
    Serial.concat(voltageY); Serial.println(" V");
  } 
  else if (voltageX > MIN_VOLTAGE_THRESHOLD && voltageY > MIN_VOLTAGE_THRESHOLD) {
    Serial.print("????? ?????????? / ??????????! ??????? X: ");
    Serial.print(voltageX, 1); Serial.print("V, ??????? Y: "); Serial.println(voltageY, 1);
  } 
  else {
    Serial.println("???? (????? ?????????)");
  }

  delay(300);
}
