# Fritzing sketch MN-82 UPG A-Sheeld (saved by Fritzing 1.0.6)
circuit board: 4cm x 4.8cm
breadboards: 1

parts:
  J1 = female pin header, 5 pins [form="♀ (female)"]
  Q1 = PNP-Transistor [package="TO92 [THT]"]
  Q2 = PNP-Transistor [package="TO92 [THT]"]
  Q3 = PNP-Transistor [package="TO92 [THT]"]
  Q4 = PNP-Transistor [package="TO92 [THT]"]
  Q5 = PNP-Transistor [package="TO92 [THT]"]
  R1 = Resistor [tolerance=±5% resistance=470 power=0.25W package=THT]
  R2 = Resistor [tolerance=±5% resistance=470 power=0.25W package=THT]
  R3 = Resistor [tolerance=±5% resistance=470 power=0.25W package=THT]
  R4 = Resistor [tolerance=±5% resistance=470 power=0.25W package=THT]
  R5 = Resistor [tolerance=±5% resistance=470 power=0.25W package=THT]
  J4 = female pin header, 2 pins [form="♀ (female)"]
  Компонент1 = Arduino Pro Mini v13
  J2 = female pin header, 1 pin [form="♀ (female)"]
  R7 = Resistor [tolerance=±5% resistance=4.7k power=0.25W package=THT]
  R8 = Resistor [tolerance=±5% resistance=10k power=0.25W package=THT]
  R9 = Resistor [tolerance=±5% resistance=4.7k power=0.25W package=THT]
  R10 = Resistor [tolerance=±5% resistance=10k power=0.25W package=THT]
  D2 = Zener Diode [part_number=1N4732A breakdown_voltage=4.7V package="300 mil [THT]"]
  D3 = Zener Diode [part_number=1N4732A breakdown_voltage=4.7V package="300 mil [THT]"]
  J5 = female pin header, 5 pins [form="♀ (female)"]
  J3 = female pin header, 2 pins [form="♀ (female)"]
  C2 = Ceramic Capacitor [capacitance=100nF voltage=20V package="200 mil [THT, multilayer]"]
  C1 = Ceramic Capacitor [capacitance=100nF voltage=20V package="200 mil [THT, multilayer]"]

nets:
  N1: J1.pin1, Q1.E
  N2: J1.pin2, Q2.E
  N3: J1.pin3, Q3.E
  N4: J1.pin4, Q4.E
  N5: J1.pin5, Q5.E
  N6: Q1.B, R1.Pin_1
  N7: Q1.C, Q2.C, Q3.C, Q4.C, Q5.C, J4.pin2, Компонент1.VCC
  N8: Q2.B, R2.Pin_1
  N9: Q3.B, R3.Pin_1
  N10: Q4.B, R4.Pin_1
  N11: Q5.B, R5.Pin_1
  N12: R1.Pin_0, Компонент1.D7
  N13: R2.Pin_0, Компонент1.D5_PWM
  N14: R3.Pin_0, Компонент1.D4
  N15: R4.Pin_0, Компонент1.D3_PWM
  N16: R5.Pin_0, Компонент1.D2
  N17: J4.pin1, Компонент1.GND, J2.pin1, R7.Pin_0, R9.Pin_1, D2.anode, D3.anode, C2.1, C1.0
  N18: Компонент1.A2, R9.Pin_0, R10.Pin_0, D2.cathode, C2.0
  N19: Компонент1.A1, R7.Pin_1, R8.Pin_0, D3.cathode, C1.1
  N20: Компонент1.D12/MISO, J5.pin5
  N21: Компонент1.D11_PWM/MOSI, J5.pin2
  N22: Компонент1.D10_PWM/SS, J5.pin1
  N23: Компонент1.D9_PWM, J5.pin3
  N24: Компонент1.D8, J5.pin4
  N25: R8.Pin_1, J3.pin2
  N26: R10.Pin_1, J3.pin1

notes:
  Vcc
  GND
  VT
  D0
  D1
  D2
  D3

// code stored in the sketch: MN-82-A0-A3.ino
const int pinX = A0;
const int pinY = A1;

// ????? ???????? ?????????? (????? 0.5 ? ?? ??????? ??????)
const float MIN_VOLTAGE_THRESHOLD = 0.5; 

void setup() {
  Serial.begin(9600);
}

void loop() {
  // ?????? ???????? (????????? ????????????? ??? ?????? ??????????)
  int rawX = analogRead(pinX);
  int rawY = analogRead(pinY);

  // ????????? ? ???????? ?????? ?? ???????? ?????? (? ?????? ????????)
  float voltageX = (rawX * 5.0 / 1023.0) * 3.12;
  float voltageY = (rawY * 5.0 / 1023.0) * 3.12;

  Serial.print("?????????? X: "); Serial.print(voltageX, 1); Serial.print("V | ");
  Serial.print("?????????? Y: "); Serial.print(voltageY, 1); Serial.print("V -> ");

  // ?????????? ?????????
  if (voltageX > MIN_VOLTAGE_THRESHOLD && voltageY < MIN_VOLTAGE_THRESHOLD) {
    Serial.print("???????? ??????. ??????????? ??????????: ");
    Serial.concat(voltageX); Serial.println(" V");
  } 
  else if (voltageY > MIN_VOLTAGE_THRESHOLD && voltageX < MIN_VOLTAGE_THRESHOLD) {
    Serial.print("???????? ?????. ??????????? ??????????: ");
    Serial.concat(voltageY); Serial.println(" V");
  } 
  else if (voltageX > MIN_VOLTAGE_THRESHOLD && voltageY > MIN_VOLTAGE_THRESHOLD) {
    Serial.print("????? ?????????? / ??????????! ??????? X: ");
    Serial.print(voltageX, 1); Serial.print("V, ??????? Y: "); Serial.println(voltageY, 1);
  } 
  else {
    Serial.println("???? (????? ?????????)");
  }

  delay(300);
}
